# Fritzing sketch pin_diagram (saved by Fritzing 0.9.2b)
breadboards: 1

parts:
  Raspberry_Pi1 = Raspberry Pi 2
  R1 = Resistor [tolerance=±5% resistance=10k package=THT]
  S1 = Pushbutton [package="[THT]"]
  Part1 = SRF05 Ultrasonic Rangefinder
  R2 = Resistor [tolerance=±5% resistance=1k package=THT]
  R3 = Resistor [tolerance=±5% resistance=2k package=THT]

nets:
  N1: Raspberry_Pi1.3v3, S1.Pin_1, S1.Pin_2
  N2: Raspberry_Pi1.GPIO5, R2.Pin_1, R3.Pin_0
  N3: Raspberry_Pi1.GPIO13, Part1.Trig
  N4: Raspberry_Pi1.GPIO26, R1.Pin_1, S1.Pin_3, S1.Pin_4
  GND: Raspberry_Pi1.GND, R1.Pin_0, Part1.GND, R3.Pin_1
  5V: Raspberry_Pi1.5V, Part1.VCC
  N5: Part1.Echo, R2.Pin_0
